// Digital circuit ALU.dig as structural Verilog
module ALU (
  input  [15:0] Left_Hand_Bus,
  input  [15:0] Right_Hand_Bus,
  input  Carry_In,
  output [15:0] Result,
  output Carry_Out
);

  wire _74283_1_pin9, _74283_2_pin9, _74283_3_pin9;

  _74283 _74283_1 (
    .pin1(Result[1]), .pin2(Right_Hand_Bus[1]), .pin3(Left_Hand_Bus[1]), .pin4(Result[0]),
    .pin5(Left_Hand_Bus[0]), .pin6(Right_Hand_Bus[0]), .pin7(Carry_In), .pin8(1'b0), .pin9(_74283_1_pin9),
    .pin10(Result[3]), .pin11(Right_Hand_Bus[3]), .pin12(Left_Hand_Bus[3]), .pin13(Result[2]),
    .pin14(Left_Hand_Bus[2]), .pin15(Right_Hand_Bus[2]), .pin16(1'b1));
  _74283 _74283_2 (
    .pin1(Result[5]), .pin2(Right_Hand_Bus[5]), .pin3(Left_Hand_Bus[5]), .pin4(Result[4]),
    .pin5(Left_Hand_Bus[4]), .pin6(Right_Hand_Bus[4]), .pin7(_74283_1_pin9), .pin8(1'b0),
    .pin9(_74283_2_pin9), .pin10(Result[7]), .pin11(Right_Hand_Bus[7]), .pin12(Left_Hand_Bus[7]),
    .pin13(Result[6]), .pin14(Left_Hand_Bus[6]), .pin15(Right_Hand_Bus[6]), .pin16(1'b1));
  _74283 _74283_3 (
    .pin1(Result[9]), .pin2(Right_Hand_Bus[9]), .pin3(Left_Hand_Bus[9]), .pin4(Result[8]),
    .pin5(Left_Hand_Bus[8]), .pin6(Right_Hand_Bus[8]), .pin7(_74283_2_pin9), .pin8(1'b0),
    .pin9(_74283_3_pin9), .pin10(Result[11]), .pin11(Right_Hand_Bus[11]), .pin12(Left_Hand_Bus[11]),
    .pin13(Result[10]), .pin14(Left_Hand_Bus[10]), .pin15(Right_Hand_Bus[10]), .pin16(1'b1));
  _74283 _74283_4 (
    .pin1(Result[13]), .pin2(Right_Hand_Bus[13]), .pin3(Left_Hand_Bus[13]), .pin4(Result[12]),
    .pin5(Left_Hand_Bus[12]), .pin6(Right_Hand_Bus[12]), .pin7(_74283_3_pin9), .pin8(1'b0), .pin9(Carry_Out),
    .pin10(Result[15]), .pin11(Right_Hand_Bus[15]), .pin12(Left_Hand_Bus[15]), .pin13(Result[14]),
    .pin14(Left_Hand_Bus[14]), .pin15(Right_Hand_Bus[14]), .pin16(1'b1));
endmodule
